// Logisim project ALU.circ as structural Verilog: 1 circuit, main circuit ALU
module ALU (
  input  [31:0] A,
  input  [31:0] B,
  input  [3:0] \Operación ,
  output [31:0] Salida,
  output ZF,
  output NF,
  output [31:0] Hi
);

  wire comparator_1_lt, comparator_2_lt, nor_2_out;
  wire [31:0] add, \and , hi_div, hi_divu, hi_mul, hi_mulu, lo_div, lo_divu, lo_mul, lo_mulu, \nor , \or ,
       S_less, sub, U_less, \xor ;

  Adder #(.width(32)) adder_1 (.a(A), .b(B), .out(add));  // open: cin, cout
  Subtractor #(.width(32)) subtractor_1 (.a(A), .b(B), .out(sub));  // open: bin, bout
  Multiplier #(.width(32)) multiplier_1 (.a(A), .b(B), .out(lo_mul), .cout(hi_mul));  // open: cin
  Divider #(.width(32)) divider_1 (.a(A), .b(B), .out(lo_div), .rem(hi_div));  // open: upper
  Comparator #(.width(32)) comparator_1 (.a(A), .b(B), .lt(comparator_1_lt));  // open: gt, eq
  Comparator #(.width(32), .mode("unsigned")) comparator_2 (.a(A), .b(B), .lt(comparator_2_lt));  // open: gt, eq
  assign S_less = {{31{1'b0}}, comparator_1_lt};  // Bit_Extender bit_extender_1
  assign U_less = {{31{1'b0}}, comparator_2_lt};  // Bit_Extender bit_extender_2
  assign \and  = A & B;  // AND_Gate and_1, 32 bits wide
  assign \or  = A | B;  // OR_Gate or_1, 32 bits wide
  assign \nor  = ~(A | B);  // NOR_Gate nor_1, 32 bits wide
  assign \xor  = A ^ B;  // XOR_Gate xor_1, 32 bits wide
  Multiplexer #(.select(4), .width(32), .enable("false")) multiplexer_1 (
    .in0(lo_mul), .in1(lo_mulu), .in2(lo_div), .in3(lo_divu), .in4(add), .in5(sub), .in6(\and ), .in7(\or ),
    .in8(\nor ), .in9(\xor ), .in10(S_less), .in11(U_less), .out(Salida), .sel(\Operación ));  // open: in12, in13, in14, in15
  Multiplexer #(.select(2), .width(32)) multiplexer_2 (
    .in0(hi_mul), .in1(hi_mulu), .in2(hi_div), .in3(hi_divu), .out(Hi), .sel(\Operación [1:0]), .en(nor_2_out));
  nor nor_2 (nor_2_out, \Operación [2], \Operación [3]);
  Comparator #(.width(32)) comparator_3 (.a(Salida), .b({32{1'b0}}), .eq(ZF), .lt(NF));  // open: gt

  // Other names for the same wires on the sheet: Op[3:0] = \Operación 

  // Notes on the sheet:
  //   Entrada
  //   Unidad Aritmético Lógica
  //   Salida
endmodule
