// Logisim project Register File.circ as structural Verilog: 1 circuit, main circuit main
module main (
  input  [31:0] IN,
  input  [4:0] SA,
  input  [4:0] SB,
  input  Reset,
  output [31:0] Out_A,
  output [31:0] Out_B
);

  wire Clk;
  wire [31:0] L0, L1, L2, L3, L4, L5, L6, L7, L8, L9, L10, L11, L12, L13, L14, L15, L16, L17, L18, L19, L20,
       L21, L22, L23, L24, L25, L26, L27, L28, L29, L30, L31;

  Clock Clock (.out(Clk));
  Multiplexer #(.select(5), .width(32)) multiplexer_1 (
    .in0(L0), .in1(L1), .in2(L2), .in3(L3), .in4(L4), .in5(L5), .in6(L6), .in7(L7), .in8(L8), .in9(L9),
    .in10(L10), .in11(L11), .in12(L12), .in13(L13), .in14(L14), .in15(L15), .in16(L16), .in17(L17),
    .in18(L18), .in19(L19), .in20(L20), .in21(L21), .in22(L22), .in23(L23), .in24(L24), .in25(L25),
    .in26(L26), .in27(L27), .in28(L28), .in29(L29), .in30(L30), .in31(L31), .out(Out_A), .sel(SA));  // open: en
  Multiplexer #(.select(5), .width(32)) multiplexer_2 (
    .in0(L0), .in1(L1), .in2(L2), .in3(L3), .in4(L4), .in5(L5), .in6(L6), .in7(L7), .in8(L8), .in9(L9),
    .in10(L10), .in11(L11), .in12(L12), .in13(L13), .in14(L14), .in15(L15), .in16(L16), .in17(L17),
    .in18(L18), .in19(L19), .in20(L20), .in21(L21), .in22(L22), .in23(L23), .in24(L24), .in25(L25),
    .in26(L26), .in27(L27), .in28(L28), .in29(L29), .in30(L30), .in31(L31), .out(Out_B), .sel(SB));  // open: en

  // Notes on the sheet:
  //   Entrada
  //   Registro de Archivos
  //   A
  //   B
endmodule
