// Logisim project S-MIPS.circ as structural Verilog: 13 circuits, main circuit Register File
module S_MIPS_Board (
  input  DESHABILITAR_DISPATCHER,
  output halt
);

  wire button_1_out, CLK, CS, d_ff_1_q, LCLR, LoadRAM, LoadRAMOn, LW, R_R_W, R_W, ram_dispatcher_1_finished,
       RCS, Reset_out, RST, TTY_EN;
  wire [2:0] KDB;
  wire [3:0] LMask, Mask, ram_1_read_time, ram_1_write_time, RMask;
  wire [6:0] KDB_DATA, TTY_DATA;
  wire [15:0] Addr, LAddr, RAddr;
  wire [31:0] I0, I1, I2, I3, LData, ram_1_data_out_0, ram_1_data_out_1, ram_1_data_out_2, ram_1_data_out_3,
       RI0, RI1, RI2, RI3;

  TTY #(.rows(25), .cols(80)) tty_1 (.data(TTY_DATA), .clk(CLK), .we(TTY_EN), .clr(RST));
  not not_1 (LoadRAMOn, ram_dispatcher_1_finished);
  RAM_Dispatcher ram_dispatcher_1 (
    .WriteTime(ram_1_write_time), .Clock(CLK), .CLR(LCLR), .Data(LData), .Address(LAddr), .Mask(LMask),
    .Finished(ram_dispatcher_1_finished), .Write(LW));
  Keyboard #(.buflen(64)) keyboard_1 (.clk(CLK), .re(KDB[0]), .avail(KDB[2]), .data(KDB_DATA));  // open: clr
  RAM ram_1 (
    .Address(RAddr), .Data_Out_0(ram_1_data_out_0), .Data_Out_1(ram_1_data_out_1),
    .Data_Out_2(ram_1_data_out_2), .Data_Out_3(ram_1_data_out_3), .Data_In_0(RI0), .Data_In_1(RI1),
    .Data_In_2(RI2), .Data_In_3(RI3), .Mask(RMask), .nRead_Write(R_R_W), .Chip_Select(RCS),
    .Read_Time(ram_1_read_time), .Write_Time(ram_1_write_time), .Reset(button_1_out));
  Button button_1 (.out(button_1_out));
  D_Flip_Flop d_ff_1 (.clk(CLK), .D(1'b1), .Q(d_ff_1_q), .reset(Reset_out));  // open: Qn, preset, en
  Button Reset (.out(Reset_out));
  S_MIPS s_mips_1 (
    .Kbd_Enable(KDB[0]), .Address(Addr), .Kbd_Clear(KDB[1]), .Kbd_Available(KDB[2]),
    .Kbd_ASCII_Data(KDB_DATA), .RAM_Out_0(ram_1_data_out_0), .TTY_Enable(TTY_EN),
    .RAM_Out_1(ram_1_data_out_1), .TTY_ASCII_Data(TTY_DATA), .Reset(RST), .RAM_Out_2(ram_1_data_out_2),
    .Clock(CLK), .Stop(halt), .RAM_Out_3(ram_1_data_out_3), .RAM_In_0(I0), .RAM_In_1(I1), .RAM_In_2(I2),
    .RAM_In_3(I3), .Mask(Mask), .Read_Time(ram_1_read_time), .Write_Time(ram_1_write_time),
    .nRead_Write(R_W), .Chip_Select(CS));
  D_Flip_Flop d_ff_2 (.clk(CLK), .D(d_ff_1_q), .Qn(LCLR), .reset(Reset_out));  // open: Q, preset, en
  or or_1 (RST, LCLR, LoadRAM);
  Clock clock_1 (.out(CLK));
  Multiplexer #(.width(32), .enable("false")) multiplexer_1 (.in0(I0), .in1(LData), .out(RI0), .sel(LoadRAM));
  Multiplexer #(.width(32), .enable("false")) multiplexer_2 (.in0(I1), .in1(LData), .out(RI1), .sel(LoadRAM));
  Multiplexer #(.width(32), .enable("false")) multiplexer_3 (.in0(I2), .in1(LData), .out(RI2), .sel(LoadRAM));
  Multiplexer #(.width(32), .enable("false")) multiplexer_4 (.in0(I3), .in1(LData), .out(RI3), .sel(LoadRAM));
  and and_1 (LoadRAM, ~DESHABILITAR_DISPATCHER, LoadRAMOn);  // AND_Gate
  Multiplexer #(.width(16), .enable("false")) multiplexer_5 (.in0(Addr), .in1(LAddr), .out(RAddr), .sel(LoadRAM));
  Multiplexer #(.width(4), .enable("false")) multiplexer_6 (.in0(Mask), .in1(LMask), .out(RMask), .sel(LoadRAM));
  Multiplexer #(.enable("false")) multiplexer_7 (.in0(CS), .in1(LW), .out(RCS), .sel(LoadRAM));
  Multiplexer #(.enable("false")) multiplexer_8 (.in0(R_W), .in1(LW), .out(R_R_W), .sel(LoadRAM));

  // Notes on the sheet:
  //   NO MODIFICAR
  //   Keyboard
endmodule

module S_MIPS (
  input  Kbd_Available,
  input  [6:0] Kbd_ASCII_Data,
  input  [31:0] RAM_Out_0,
  input  [31:0] RAM_Out_1,
  input  Reset,
  input  [31:0] RAM_Out_2,
  input  Clock,
  input  [31:0] RAM_Out_3,
  input  [3:0] Read_Time,
  input  [3:0] Write_Time,
  output Kbd_Enable,
  output [15:0] Address,
  output Kbd_Clear,
  output TTY_Enable,
  output [6:0] TTY_ASCII_Data,
  output Stop,
  output [31:0] RAM_In_0,
  output [31:0] RAM_In_1,
  output [31:0] RAM_In_2,
  output [31:0] RAM_In_3,
  output [3:0] Mask,
  output nRead_Write,
  output Chip_Select
);

  Data_Path data_path_1 (
    .in_1(RAM_Out_0), .in_2(RAM_Out_1), .in_3(RAM_Out_2), .in_4(RAM_Out_3), .in_6(Reset), .in_7(Clock),
    .in_12(Read_Time));  // open: in_5, in_8, in_9, in_10, in_11, Ram_Address, Memory_Data, Ram_Data_Write, out_16, out_17, out_18, out_19, out_20, out_21, out_22

  // Other names for the same wires on the sheet: CLK = Clock; CLR = Reset; CS = Chip_Select;
  //   KBD_AVAIL = Kbd_Available; KBD_CLR = Kbd_Clear; KBD_DATA[6:0] = Kbd_ASCII_Data; RAM_A[15:0] = Address;
  //   RAM_INPUT_0[31:0] = RAM_In_0; RAM_INPUT_1[31:0] = RAM_In_1; RAM_INPUT_2[31:0] = RAM_In_2;
  //   RAM_INPUT_3[31:0] = RAM_In_3; RAM_MASK[3:0] = Mask; RAM_OUTPUT_0[31:0] = RAM_Out_0;
  //   RAM_OUTPUT_1[31:0] = RAM_Out_1; RAM_OUTPUT_2[31:0] = RAM_Out_2; RAM_OUTPUT_3[31:0] = RAM_Out_3;
  //   RW = nRead_Write; TTY_DATA[6:0] = TTY_ASCII_Data

  // Notes on the sheet:
  //   RAM ADDRESS
  //   DATA FROM RAM
  //   DATA TO RAM
  //   DATA WRITE MASK
  //   RAM TIMING
  //   RAM CONTROL
  //   KEYBOARD
  //   TTY
  //   SEQUENCING
endmodule

module RAM (
  input  [15:0] Address,
  input  [31:0] Data_In_0,
  input  [31:0] Data_In_1,
  input  [31:0] Data_In_2,
  input  [31:0] Data_In_3,
  input  [3:0] Mask,
  input  nRead_Write,
  input  Chip_Select,
  input  Reset,
  output [31:0] Data_Out_0,
  output [31:0] Data_Out_1,
  output [31:0] Data_Out_2,
  output [31:0] Data_Out_3,
  output [3:0] Read_Time,
  output [3:0] Write_Time
);

  wire and_2_out, and_3_out, and_4_out, and_5_out, and_6_out, and_7_out, and_8_out, and_9_out, Changed, CLK,
       comparator_2_eq, comparator_3_eq, comparator_4_eq, comparator_5_eq, comparator_6_eq, Count,
       demultiplexer_3_out0, Idle, Idle_q, Load, Load0, Load1, nand_1_out, or_1_out, or_2_out, or_3_out,
       or_4_out, or_5_out, or_6_out, or_7_out, or_8_out, or_9_out, or_10_out, Proc_q, Update_Mem, Zero_Time;
  wire [3:0] counter_1_q, multiplexer_1_out, subtractor_1_out;
  wire [31:0] register_1_q, register_2_q, register_3_q, register_4_q, register_5_q;

  // Probe on 4'b0011
  // Probe on 4'b0010
  Multiplexer #(.width(4), .enable("false")) multiplexer_1 (
    .in0(4'b0011), .in1(4'b0010), .out(multiplexer_1_out), .sel(nRead_Write));
  or or_1 (or_1_out, Idle, Update_Mem);
  or or_2 (or_2_out, ~Chip_Select, Reset);  // OR_Gate
  Subtractor #(.width(4)) subtractor_1 (.a(multiplexer_1_out), .b(4'b0010), .out(subtractor_1_out));  // open: bin, bout
  Demultiplexer #(.enable("false")) demultiplexer_1 (.out0(Idle), .out1(Load0), .in(Idle_q), .sel(Changed));
  D_Flip_Flop u_Idle (.clk(CLK), .D(or_1_out), .Q(Idle_q), .preset(or_2_out));  // open: Qn, en, reset
  // Probe on counter_1_q
  Counter #(.width(4), .max('hf)) counter_1 (
    .load(Load), .D(subtractor_1_out), .count(Count), .Q(counter_1_q), .clk(CLK), .clr(or_3_out));  // open: carry
  or or_3 (or_3_out, ~Chip_Select, Reset);  // OR_Gate
  Comparator #(.width(4), .mode("unsigned")) comparator_1 (
    .a(4'b0000), .b(counter_1_q), .eq(Zero_Time));  // open: gt, lt
  or or_4 (or_4_out, Count, Load0, Load1);
  Register #(.width(32)) register_1 (.D(Data_In_0), .en(Chip_Select), .Q(register_1_q), .clk(CLK), .clr(or_5_out));
  or or_5 (or_5_out, ~Chip_Select, Reset);  // OR_Gate
  Register #(.width(32)) register_2 (.D(Data_In_1), .en(Chip_Select), .Q(register_2_q), .clk(CLK), .clr(or_6_out));
  or or_6 (or_6_out, ~Chip_Select, Reset);  // OR_Gate
  Register #(.width(32)) register_3 (.D(Data_In_2), .en(Chip_Select), .Q(register_3_q), .clk(CLK), .clr(or_7_out));
  or or_7 (or_7_out, ~Chip_Select, Reset);  // OR_Gate
  Register #(.width(32)) register_4 (.D(Data_In_3), .en(Chip_Select), .Q(register_4_q), .clk(CLK), .clr(or_8_out));
  or or_8 (or_8_out, ~Chip_Select, Reset);  // OR_Gate
  Register #(.width(32)) register_5 (
    .D({{11{1'b1}}, nRead_Write, Mask, Address}), .en(Chip_Select), .Q(register_5_q), .clk(CLK),
    .clr(or_9_out));
  or or_9 (or_9_out, ~Chip_Select, Reset);  // OR_Gate
  D_Flip_Flop Proc (.clk(CLK), .D(or_4_out), .Q(Proc_q), .reset(or_10_out));  // open: Qn, preset, en
  or or_10 (or_10_out, ~Chip_Select, Reset);  // OR_Gate
  Demultiplexer #(.enable("false")) demultiplexer_2 (
    .out0(Count), .out1(Update_Mem), .in(demultiplexer_3_out0), .sel(Zero_Time));
  Demultiplexer #(.enable("false")) demultiplexer_3 (
    .out0(demultiplexer_3_out0), .out1(Load1), .in(Proc_q), .sel(Changed));
  Clock clock_1 (.out(CLK));
  Comparator #(.width(32)) comparator_2 (.a(register_1_q), .b(Data_In_0), .eq(comparator_2_eq));  // open: gt, lt
  Comparator #(.width(32)) comparator_3 (.a(register_2_q), .b(Data_In_1), .eq(comparator_3_eq));  // open: gt, lt
  Comparator #(.width(32)) comparator_4 (.a(register_3_q), .b(Data_In_2), .eq(comparator_4_eq));  // open: gt, lt
  Comparator #(.width(32)) comparator_5 (.a(register_4_q), .b(Data_In_3), .eq(comparator_5_eq));  // open: gt, lt
  Comparator #(.width(32)) comparator_6 (
    .a(register_5_q), .b({{11{1'b1}}, nRead_Write, Mask, Address}), .eq(comparator_6_eq));  // open: gt, lt
  nand nand_1 (nand_1_out, comparator_6_eq, comparator_2_eq, comparator_3_eq, comparator_4_eq, comparator_5_eq);
  and and_1 (Changed, nand_1_out, Chip_Select);
  or or_11 (Load, Count, Load1, Load0);
  and and_2 (and_2_out, Mask[0], Update_Mem, nRead_Write);
  and and_3 (and_3_out, Mask[1], Update_Mem, nRead_Write);
  and and_4 (and_4_out, Mask[2], Update_Mem, nRead_Write);
  and and_5 (and_5_out, Mask[3], Update_Mem, nRead_Write);
  RAM_part #(.addrWidth(16), .dataWidth(32), .bus("separate")) ram_1 (
    .addr(Address), .din(Data_In_0), .data(Data_Out_0), .str(and_2_out), .sel(Chip_Select), .clk(CLK),
    .ld(and_6_out), .clr(Reset));
  and and_6 (and_6_out, ~nRead_Write, Idle);  // AND_Gate
  RAM_part #(.addrWidth(16), .dataWidth(32), .bus("separate")) ram_2 (
    .addr(Address), .din(Data_In_1), .data(Data_Out_1), .str(and_3_out), .sel(Chip_Select), .clk(CLK),
    .ld(and_7_out), .clr(Reset));
  and and_7 (and_7_out, ~nRead_Write, Idle);  // AND_Gate
  RAM_part #(.addrWidth(16), .dataWidth(32), .bus("separate")) ram_3 (
    .addr(Address), .din(Data_In_2), .data(Data_Out_2), .str(and_4_out), .sel(Chip_Select), .clk(CLK),
    .ld(and_8_out), .clr(Reset));
  and and_8 (and_8_out, ~nRead_Write, Idle);  // AND_Gate
  RAM_part #(.addrWidth(16), .dataWidth(32), .bus("separate")) ram_4 (
    .addr(Address), .din(Data_In_3), .data(Data_Out_3), .str(and_5_out), .sel(Chip_Select), .clk(CLK),
    .ld(and_9_out), .clr(Reset));
  and and_9 (and_9_out, ~nRead_Write, Idle);  // AND_Gate

  assign Read_Time = 4'b0011;
  assign Write_Time = 4'b0010;

  // Other names for the same wires on the sheet: M0 = Mask[0]; M1 = Mask[1]; M2 = Mask[2]; M3 = Mask[3];
  //   RW = nRead_Write; CLR = Reset; CS = Chip_Select; Load2 = Count

  // Notes on the sheet:
  //   NO MODIFICAR
  //   excepto quizás los valores RT y WT
  //   BANK0
  //   BANK1
  //   BANK2
  //   BANK3
endmodule

module RAM_Dispatcher (
  input  [3:0] WriteTime,
  input  Clock,
  input  CLR,
  output [31:0] Data,
  output [15:0] Address,
  output [3:0] Mask,
  output Finished,
  output Write
);

  wire demultiplexer_2_out1, demultiplexer_3_out1, End, IDLE_q, IncAddr, Load, or_1_out, or_2_out, While_q,
       WriteEnd;
  wire [3:0] counter_1_q;
  wire [31:0] CurrentAddress_q;

  Counter #(.width(32), .max('hffffffff)) CurrentAddress (
    .count(IncAddr), .Q({CurrentAddress_q[31:18], Address, CurrentAddress_q[1:0]}), .clk(Clock), .clr(CLR));  // open: load, D, carry
  or or_1 (or_1_out, IncAddr, demultiplexer_3_out1, Finished);
  D_Flip_Flop IDLE (.clk(Clock), .D(or_1_out), .Q(IDLE_q), .preset(CLR));  // open: Qn, en, reset
  Demultiplexer #(.enable("false")) demultiplexer_1 (.out0(Load), .out1(Finished), .in(IDLE_q), .sel(End));
  D_Flip_Flop While (.clk(Clock), .D(or_2_out), .Q(While_q), .reset(CLR));  // open: Qn, preset, en
  or or_2 (or_2_out, Write, Load);
  RAM_part #(.addrWidth(18), .dataWidth(32)) ram_1 (
    .addr({Address, CurrentAddress_q[1:0]}), .data(Data), .clk(Clock));  // open: sel, ld, clr
  Demultiplexer #(.enable("false")) demultiplexer_2 (
    .out0(Write), .out1(demultiplexer_2_out1), .in(While_q), .sel(WriteEnd));
  Decoder #(.select(2)) decoder_1 (
    .out0(Mask[0]), .out1(Mask[1]), .out2(Mask[2]), .out3(Mask[3]), .sel(CurrentAddress_q[1:0]));  // open: en
  Demultiplexer #(.enable("false")) demultiplexer_3 (
    .out0(IncAddr), .out1(demultiplexer_3_out1), .in(demultiplexer_2_out1), .sel(End));
  Counter #(.width(4), .max('hf)) counter_1 (
    .load(Load), .D(WriteTime), .count(Write), .Q(counter_1_q), .clk(Clock));  // open: carry, clr
  Comparator #(.width(32)) comparator_1 (.a(Data), .b({32{1'b1}}), .eq(End));  // open: gt, lt
  Comparator #(.width(4)) comparator_2 (.a(4'b0000), .b(counter_1_q), .eq(WriteEnd));  // open: gt, lt

  // Other names for the same wires on the sheet: CLK = Clock; Count = Write; WT[3:0] = WriteTime
endmodule

module Data_Path (
  input  [31:0] in_1,
  input  [31:0] in_2,
  input  [31:0] in_3,
  input  [31:0] in_4,
  input  [31:0] in_5,
  input  in_6,
  input  in_7,
  input  in_8,
  input  in_9,
  input  in_10,
  input  [1:0] in_11,
  input  [3:0] in_12,
  output [15:0] Ram_Address,
  output [31:0] Memory_Data,
  output [31:0] Ram_Data_Write,
  output out_16,
  output out_17,
  output out_18,
  output out_19,
  output out_20,
  output [1:0] out_21,
  output [3:0] out_22
);

  wire E, M, N, P, R_W, S_H_L, Z;
  wire [2:0] B_Op;
  wire [3:0] A_Op;
  wire [4:0] DataAddress, Selector_A, Selector_B;
  wire [15:0] Ram_addr;
  wire [25:0] Jump;
  wire [31:0] B, carry, Cnst, Data_In, Hi_Lo, Instruction, kbd, multiplexer_1_out, multiplexer_3_out, Out,
       out_t, PC, PC_new;

  Register #(.width(32)) Program_Counter (.D(PC_new), .en(in_10), .Q(PC), .clk(in_7), .clr(in_6));
  Register_File register_file_1 (
    .DI(Data_In), .R_W(R_W), .Rd(DataAddress), .Rs(Selector_A), .Rt(Selector_B), .Clk(in_7), .Reset(in_6),
    .DRs(Ram_Data_Write), .DRt(B), .Load(in_8), .Hi_Lo(Hi_Lo), .Select(S_H_L), .L(out_t), .H(carry));
  Cache_Memory cache_memory_1 (
    .in_1(in_1), .in_2(in_3), .in_3(in_2), .in_4(in_4), .in_7(in_7), .in_8(in_6), .in_9(in_9),
    .out_11(Instruction), .out_12(Ram_addr), .R_W_Ram(out_18), .Data_Ready(out_16), .Addr(PC),
    .Ram_Load(out_20), .in_10(in_12));  // open: W_Ram
  Branch_Control branch_control_1 (
    .PC(PC), .Const(Cnst), .N(N), .Z(Z), .B_Op(B_Op), .PC_out(PC_new), .Destiny(Jump), .P(P), .Equal(E));
  Multiplexer #(.width(32), .enable("false")) multiplexer_1 (
    .in0(Ram_Data_Write), .in1(B), .out(multiplexer_1_out), .sel(out_17));
  Multiplexer #(.select(2), .width(32), .enable("false")) multiplexer_2 (
    .in0(Out), .in2(kbd), .out(Data_In), .sel(in_11));  // open: in1, in3
  Multiplexer #(.width(32), .enable("false")) multiplexer_3 (
    .in0(multiplexer_1_out), .in1(Hi_Lo), .out(multiplexer_3_out), .sel(M));
  ALU alu_1 (
    .A(multiplexer_3_out), .Operation(A_Op), .out(out_t), .ZF(Z), .NF(N), .Hi(carry), .PF(P), .Equal(E));  // open: B
  Intruction_Decoder intruction_decoder_1 (
    .Constant(Cnst), .Jump(Jump), .Unit_Op(out_22), .ALU_Op(A_Op), .Branch_Op(B_Op), .Special_Op(out_21),
    .S_A(Selector_A), .S_B(Selector_B), .DA(DataAddress), .Move_Lo_Hi(S_H_L), .pop_push(out_17),
    .load_store(out_19), .Intruction(Instruction));
  Multiplexer #(.width(32), .enable("false")) multiplexer_4 (
    .in0(B), .in1(Ram_Data_Write), .out(Memory_Data), .sel(out_17));

  // Other names for the same wires on the sheet: A[31:0] = Ram_Data_Write; Address[15:0] = Ram_Address; Clk = in_7;
  //   End = out_16; In0[31:0] = in_1; In1[31:0] = in_2; In2[31:0] = in_3; In3[31:0] = in_4; Kybd[31:0] = in_5;
  //   Load_Ram = out_20; Load_Store = out_19; P_P = out_17; PC_Enable = in_10; Ram_R_W = out_18;
  //   Read_Time[3:0] = in_12; Reset = in_6; RW = in_8; RW_Cache = in_9; S_Data[1:0] = in_11; Special_Op[1:0] = out_21;
  //   Unit_Op[3:0] = out_22

  // Notes on the sheet:
  //   Inputs
  //   Data Path
  //   Outputs
endmodule

module ALU (
  input  [31:0] A,
  input  [31:0] B,
  input  [3:0] Operation,
  output [31:0] out,
  output PF,
  output ZF,
  output NF,
  output Equal,
  output [31:0] Hi
);

  wire comparator_1_lt, comparator_2_lt, nor_2_out;
  wire [31:0] add, \and , hi_div, hi_divu, hi_mul, hi_mulu, lo_div, lo_divu, lo_mul, lo_mulu, \nor , \or ,
       S_less, sub, U_less, \xor ;

  Multiplier #(.width(32)) multiplier_1 (.a(A), .b(B), .out(lo_mul), .cout(hi_mul));  // open: cin
  Mulu mulu_1 (.A(A), .B(B), .Lo(lo_mulu), .Hi(hi_mulu));
  Div div_1 (.A(A), .B(B), .Lo(lo_div), .Hi(hi_div));
  Comparator #(.width(32)) comparator_1 (.a(A), .b(B), .eq(Equal), .lt(comparator_1_lt));  // open: gt
  assign S_less = {{31{1'b0}}, comparator_1_lt};  // Bit_Extender bit_extender_1
  Adder #(.width(32)) adder_1 (.a(A), .b(B), .out(add));  // open: cin, cout
  Subtractor #(.width(32)) subtractor_1 (.a(A), .b(B), .out(sub));  // open: bin, bout
  Divider #(.width(32)) divider_1 (.a(A), .b(B), .out(lo_divu), .rem(hi_divu));  // open: upper
  assign \and  = A & B;  // AND_Gate and_1, 32 bits wide
  assign \or  = A | B;  // OR_Gate or_1, 32 bits wide
  Comparator #(.width(32), .mode("unsigned")) comparator_2 (.a(A), .b(B), .lt(comparator_2_lt));  // open: gt, eq
  assign U_less = {{31{1'b0}}, comparator_2_lt};  // Bit_Extender bit_extender_2
  assign \nor  = ~(A | B);  // NOR_Gate nor_1, 32 bits wide
  assign \xor  = A ^ B;  // XOR_Gate xor_1, 32 bits wide
  Multiplexer #(.select(4), .width(32), .enable("false")) multiplexer_1 (
    .in0(lo_mul), .in1(lo_mulu), .in2(lo_div), .in3(lo_divu), .in4(add), .in5(sub), .in6(\and ), .in7(\or ),
    .in8(\nor ), .in9(\xor ), .in10(S_less), .in11(U_less), .in12(A), .out(out), .sel(Operation));  // open: in13, in14, in15
  Multiplexer #(.select(2), .width(32)) multiplexer_2 (
    .in0(hi_mul), .in1(hi_mulu), .in2(hi_div), .in3(hi_divu), .out(Hi), .sel(Operation[1:0]), .en(nor_2_out));
  nor nor_2 (nor_2_out, Operation[2], Operation[3]);
  Comparator #(.width(32)) comparator_3 (.a(out), .b({32{1'b0}}), .gt(PF), .eq(ZF), .lt(NF));

  // Other names for the same wires on the sheet: Op[3:0] = Operation

  // Notes on the sheet:
  //   Inputs
  //   Aritmetic Logic Unit
  //   Outputs
endmodule

module Mulu (
  input  [31:0] A,
  input  [31:0] B,
  output [31:0] Lo,
  output [31:0] Hi
);

  wire [31:0] adder_1_out, multiplexer_1_out, multiplexer_2_out, multiplier_1_cout;

  Multiplexer #(.width(32), .enable("false")) multiplexer_1 (
    .in0({32{1'b0}}), .in1(A), .out(multiplexer_1_out), .sel(B[31]));
  Multiplexer #(.width(32), .enable("false")) multiplexer_2 (
    .in0({32{1'b0}}), .in1(B), .out(multiplexer_2_out), .sel(A[31]));
  Adder #(.width(32)) adder_1 (.a(multiplexer_1_out), .b(multiplexer_2_out), .out(adder_1_out));  // open: cin, cout
  Multiplier #(.width(32)) multiplier_1 (.a(A), .b(B), .out(Lo), .cout(multiplier_1_cout));  // open: cin
  Adder #(.width(32)) adder_2 (.a(multiplier_1_cout), .b(adder_1_out), .out(Hi));  // open: cin, cout
endmodule

module Div (
  input  [31:0] A,
  input  [31:0] B,
  output [31:0] Lo,
  output [31:0] Hi
);

  wire xor_1_out;
  wire [31:0] divider_1_out, multiplexer_1_out, multiplexer_2_out, negator_1_out, negator_2_out,
       negator_3_out;

  Negator #(.width(32)) negator_1 (.in(A), .out(negator_1_out));
  Negator #(.width(32)) negator_2 (.in(B), .out(negator_2_out));
  Multiplexer #(.width(32), .enable("false")) multiplexer_1 (
    .in0(A), .in1(negator_1_out), .out(multiplexer_1_out), .sel(A[31]));
  Multiplexer #(.width(32), .enable("false")) multiplexer_2 (
    .in0(B), .in1(negator_2_out), .out(multiplexer_2_out), .sel(B[31]));
  Divider #(.width(32)) divider_1 (
    .a(multiplexer_1_out), .b(multiplexer_2_out), .out(divider_1_out), .rem(Hi));  // open: upper
  xor xor_1 (xor_1_out, A[31], B[31]);
  Negator #(.width(32)) negator_3 (.in(divider_1_out), .out(negator_3_out));
  Multiplexer #(.width(32), .enable("false")) multiplexer_3 (
    .in0(divider_1_out), .in1(negator_3_out), .out(Lo), .sel(xor_1_out));
endmodule

module Register_File (
  input  [31:0] DI,
  input  R_W,
  input  [4:0] Rd,
  input  [4:0] Rs,
  input  [4:0] Rt,
  input  Clk,
  input  Reset,
  input  [31:0] L,
  input  [31:0] H,
  input  Load,
  input  Select,
  output [31:0] DRs,
  output [31:0] DRt,
  output [31:0] Hi_Lo
);

  wire L0, L1, L2, L3, L4, L5, L6, L7, L8, L9, L10, L11, L12, L13, L14, L15, L16, L17, L18, L19, L20, L21,
       L22, L23, L24, L25, L26, L27, L28, L29, L30, LSP;
  wire [31:0] Hi, Lo, Q0, Q1, Q2, Q3, Q4, Q5, Q6, Q7, Q8, Q9, Q10, Q11, Q12, Q13, Q14, Q15, Q16, Q17, Q18,
       Q19, Q20, Q21, Q22, Q23, Q24, Q25, Q26, Q27, Q28, Q29, Q30, QSP;

  Register #(.width(32)) R0 (.Q(Q0), .clk(Clk), .clr(Reset));  // open: D, en
  Register #(.width(32)) R6 (.D(DI), .en(L6), .Q(Q6), .clk(Clk), .clr(Reset));
  Register #(.width(32)) R12 (.D(DI), .en(L12), .Q(Q12), .clk(Clk), .clr(Reset));
  Register #(.width(32)) R18 (.D(DI), .en(L18), .Q(Q18), .clk(Clk), .clr(Reset));
  Register #(.width(32)) R24 (.D(DI), .en(L24), .Q(Q24), .clk(Clk), .clr(Reset));
  Register #(.width(32)) R30 (.D(DI), .en(L30), .Q(Q30), .clk(Clk), .clr(Reset));
  Register #(.width(32)) u_Lo (.D(L), .en(Load), .Q(Lo), .clk(Clk), .clr(Reset));
  Register #(.width(32)) R1 (.D(DI), .en(L1), .Q(Q1), .clk(Clk), .clr(Reset));
  Register #(.width(32)) R7 (.D(DI), .en(L7), .Q(Q7), .clk(Clk), .clr(Reset));
  Register #(.width(32)) R13 (.D(DI), .en(L13), .Q(Q13), .clk(Clk), .clr(Reset));
  Register #(.width(32)) R19 (.D(DI), .en(L19), .Q(Q19), .clk(Clk), .clr(Reset));
  Register #(.width(32)) R25 (.D(DI), .en(L25), .Q(Q25), .clk(Clk), .clr(Reset));
  Register #(.width(32)) SP ();  // open: D, en, Q, clk, clr
  Register #(.width(32)) u_Hi (.D(H), .en(Load), .Q(Hi), .clk(Clk), .clr(Reset));
  Register #(.width(32)) R2 (.D(DI), .en(L2), .Q(Q2), .clk(Clk), .clr(Reset));
  Register #(.width(32)) R8 (.D(DI), .en(L8), .Q(Q8), .clk(Clk), .clr(Reset));
  Register #(.width(32)) R14 (.D(DI), .en(L14), .Q(Q14), .clk(Clk), .clr(Reset));
  Register #(.width(32)) R20 (.D(DI), .en(L20), .Q(Q20), .clk(Clk), .clr(Reset));
  Register #(.width(32)) R26 (.D(DI), .en(L26), .Q(Q26), .clk(Clk), .clr(Reset));
  Register #(.width(32)) R3 (.D(DI), .en(L3), .Q(Q3), .clk(Clk), .clr(Reset));
  Register #(.width(32)) R9 (.D(DI), .en(L9), .Q(Q9), .clk(Clk), .clr(Reset));
  Register #(.width(32)) R15 (.D(DI), .en(L15), .Q(Q15), .clk(Clk), .clr(Reset));
  Register #(.width(32)) R21 (.D(DI), .en(L21), .Q(Q21), .clk(Clk), .clr(Reset));
  Register #(.width(32)) R27 (.D(DI), .en(L27), .Q(Q27), .clk(Clk), .clr(Reset));
  Register #(.width(32)) R4 (.D(DI), .en(L4), .Q(Q4), .clk(Clk), .clr(Reset));
  Register #(.width(32)) R10 (.D(DI), .en(L10), .Q(Q10), .clk(Clk), .clr(Reset));
  Register #(.width(32)) R16 (.D(DI), .en(L16), .Q(Q16), .clk(Clk), .clr(Reset));
  Register #(.width(32)) R22 (.D(DI), .en(L22), .Q(Q22), .clk(Clk), .clr(Reset));
  Register #(.width(32)) R28 (.D(DI), .en(L28), .Q(Q28), .clk(Clk), .clr(Reset));
  Register #(.width(32)) R5 (.D(DI), .en(L5), .Q(Q5), .clk(Clk), .clr(Reset));
  Register #(.width(32)) R11 (.D(DI), .en(L11), .Q(Q11), .clk(Clk), .clr(Reset));
  Register #(.width(32)) R17 (.D(DI), .en(L17), .Q(Q17), .clk(Clk), .clr(Reset));
  Register #(.width(32)) R23 (.D(DI), .en(L23), .Q(Q23), .clk(Clk), .clr(Reset));
  Register #(.width(32)) R29 (.D(DI), .en(L29), .Q(Q29), .clk(Clk), .clr(Reset));
  Demultiplexer #(.select(5)) demultiplexer_1 (
    .out0(L0), .out1(L1), .out2(L2), .out3(L3), .out4(L4), .out5(L5), .out6(L6), .out7(L7), .out8(L8),
    .out9(L9), .out10(L10), .out11(L11), .out12(L12), .out13(L13), .out14(L14), .out15(L15), .out16(L16),
    .out17(L17), .out18(L18), .out19(L19), .out20(L20), .out21(L21), .out22(L22), .out23(L23), .out24(L24),
    .out25(L25), .out26(L26), .out27(L27), .out28(L28), .out29(L29), .out30(L30), .out31(LSP), .in(R_W),
    .sel(Rd));  // open: en
  Multiplexer #(.select(5), .width(32)) multiplexer_1 (
    .in0(Q0), .in1(Q1), .in2(Q2), .in3(Q3), .in4(Q4), .in5(Q5), .in6(Q6), .in7(Q7), .in8(Q8), .in9(Q9),
    .in10(Q10), .in11(Q11), .in12(Q12), .in13(Q13), .in14(Q14), .in15(Q15), .in16(Q16), .in17(Q17),
    .in18(Q18), .in19(Q19), .in20(Q20), .in21(Q21), .in22(Q22), .in23(Q23), .in24(Q24), .in25(Q25),
    .in26(Q26), .in27(Q27), .in28(Q28), .in29(Q29), .in30(Q30), .in31(QSP), .out(DRs), .sel(Rs));  // open: en
  Multiplexer #(.select(5), .width(32)) multiplexer_2 (
    .in0(Q0), .in1(Q1), .in2(Q2), .in3(Q3), .in4(Q4), .in5(Q5), .in6(Q6), .in7(Q7), .in8(Q8), .in9(Q9),
    .in10(Q10), .in11(Q11), .in12(Q12), .in13(Q13), .in14(Q14), .in15(Q15), .in16(Q16), .in17(Q17),
    .in18(Q18), .in19(Q19), .in20(Q20), .in21(Q21), .in22(Q22), .in23(Q23), .in24(Q24), .in25(Q25),
    .in26(Q26), .in27(Q27), .in28(Q28), .in29(Q29), .in30(Q30), .in31(QSP), .out(DRt), .sel(Rt));  // open: en
  Multiplexer #(.width(32), .enable("false")) multiplexer_3 (.in0(Hi), .in1(Lo), .out(Hi_Lo), .sel(Select));

  // Other names for the same wires on the sheet: LM_D = Load; Rst = Reset; Selector_H_L = Select

  // Notes on the sheet:
  //   Inputs
  //   Data in
  //   Read/Write
  //   Data Address
  //   Selector A
  //   Selector B
  //   Clock
  //   Reset
  //   Low and high
  //   Register File
  //   Outputs
  //   Data out
  //   Data out
  //   Data out
endmodule

module Cache_Memory (
  input  [31:0] in_1,
  input  [31:0] in_2,
  input  [31:0] in_3,
  input  [31:0] in_4,
  input  [31:0] Addr,
  input  [15:0] W_Ram,
  input  in_7,
  input  in_8,
  input  in_9,
  input  [3:0] in_10,
  output [31:0] out_11,
  output [15:0] out_12,
  output R_W_Ram,
  output Data_Ready,
  output Ram_Load
);

  wire comparator_1_eq, comparator_2_eq, d_ff_9_q, en0, en1, en2, en3, en4, en5, en6, en7, Invalidate,
       nor_1_out, not_1_out, or_1_out, Ram, Ready_RT, V0, V1, V2, V3, V4, V5, V6, V7, Validate, Validated,
       Validated_R;
  wire [1:0] offset_t;
  wire [2:0] multiplexer_8_out;
  wire [3:0] adder_1_out, counter_1_q, RT;
  wire [12:0] T0, T1, T2, T3, T4, T5, T6, T7, TagCopy, TagCopy_R;
  wire [31:0] multiplexer_1_out, multiplexer_2_out, multiplexer_4_out, multiplexer_5_out, O0, O1, O2, O3, O4,
       O5, O6, O7, O8, O9, O10, O11, O12, O13, O14, O15, O16, O17, O18, O19, O20, O21, O22, O23, O24, O25,
       O26, O27, O28, O29, O30, O31;

  Register #(.width(13)) register_1 (.D(Addr[19:7]), .en(en0), .Q(T0), .clk(in_7), .clr(in_8));
  Register #(.width(13)) register_2 (.D(Addr[19:7]), .en(en1), .Q(T1), .clk(in_7), .clr(in_8));
  Register #(.width(13)) register_3 (.D(Addr[19:7]), .en(en2), .Q(T2), .clk(in_7), .clr(in_8));
  Register #(.width(13)) register_4 (.D(Addr[19:7]), .en(en3), .Q(T3), .clk(in_7), .clr(in_8));
  Register #(.width(13)) register_5 (.D(Addr[19:7]), .en(en4), .Q(T4), .clk(in_7), .clr(in_8));
  Register #(.width(13)) register_6 (.D(Addr[19:7]), .en(en5), .Q(T5), .clk(in_7), .clr(in_8));
  Register #(.width(13)) register_7 (.D(Addr[19:7]), .en(en6), .Q(T6), .clk(in_7), .clr(in_8));
  Register #(.width(13)) register_8 (.D(Addr[19:7]), .en(en7), .Q(T7), .clk(in_7), .clr(in_8));
  Register #(.width(32)) register_9 (.D(in_1), .en(en0), .Q(O0), .clk(in_7), .clr(in_8));
  Register #(.width(32)) register_10 (.D(in_1), .en(en1), .Q(O4), .clk(in_7), .clr(in_8));
  Register #(.width(32)) register_11 (.D(in_1), .en(en2), .Q(O8), .clk(in_7), .clr(in_8));
  Register #(.width(32)) register_12 (.D(in_1), .en(en3), .Q(O12), .clk(in_7), .clr(in_8));
  Register #(.width(32)) register_13 (.D(in_1), .en(en4), .Q(O16), .clk(in_7), .clr(in_8));
  Register #(.width(32)) register_14 (.D(in_1), .en(en5), .Q(O20), .clk(in_7), .clr(in_8));
  Register #(.width(32)) register_15 (.D(in_1), .en(en6), .Q(O24), .clk(in_7), .clr(in_8));
  Register #(.width(32)) register_16 (.D(in_1), .en(en7), .Q(O28), .clk(in_7), .clr(in_8));
  Register #(.width(32)) register_17 (.D(in_2), .en(en0), .Q(O1), .clk(in_7), .clr(in_8));
  Register #(.width(32)) register_18 (.D(in_2), .en(en1), .Q(O5), .clk(in_7), .clr(in_8));
  Register #(.width(32)) register_19 (.D(in_2), .en(en2), .Q(O9), .clk(in_7), .clr(in_8));
  Register #(.width(32)) register_20 (.D(in_2), .en(en3), .Q(O13), .clk(in_7), .clr(in_8));
  Register #(.width(32)) register_21 (.D(in_2), .en(en4), .Q(O17), .clk(in_7), .clr(in_8));
  Register #(.width(32)) register_22 (.D(in_2), .en(en5), .Q(O21), .clk(in_7), .clr(in_8));
  Register #(.width(32)) register_23 (.D(in_2), .en(en6), .Q(O25), .clk(in_7), .clr(in_8));
  Register #(.width(32)) register_24 (.D(in_2), .en(en7), .Q(O29), .clk(in_7), .clr(in_8));
  Register #(.width(32)) register_25 (.D(in_3), .en(en0), .Q(O2), .clk(in_7), .clr(in_8));
  Register #(.width(32)) register_26 (.D(in_3), .en(en1), .Q(O6), .clk(in_7), .clr(in_8));
  Register #(.width(32)) register_27 (.D(in_3), .en(en2), .Q(O10), .clk(in_7), .clr(in_8));
  Register #(.width(32)) register_28 (.D(in_3), .en(en3), .Q(O14), .clk(in_7), .clr(in_8));
  Register #(.width(32)) register_29 (.D(in_3), .en(en4), .Q(O18), .clk(in_7), .clr(in_8));
  Register #(.width(32)) register_30 (.D(in_3), .en(en5), .Q(O22), .clk(in_7), .clr(in_8));
  Register #(.width(32)) register_31 (.D(in_3), .en(en6), .Q(O26), .clk(in_7), .clr(in_8));
  Register #(.width(32)) register_32 (.D(in_3), .en(en7), .Q(O30), .clk(in_7), .clr(in_8));
  Register #(.width(32)) register_33 (.D(in_4), .en(en0), .Q(O3), .clk(in_7), .clr(in_8));
  Register #(.width(32)) register_34 (.D(in_4), .en(en1), .Q(O7), .clk(in_7), .clr(in_8));
  Register #(.width(32)) register_35 (.D(in_4), .en(en2), .Q(O11), .clk(in_7), .clr(in_8));
  Register #(.width(32)) register_36 (.D(in_4), .en(en3), .Q(O15), .clk(in_7), .clr(in_8));
  Register #(.width(32)) register_37 (.D(in_4), .en(en4), .Q(O19), .clk(in_7), .clr(in_8));
  Register #(.width(32)) register_38 (.D(in_4), .en(en5), .Q(O23), .clk(in_7), .clr(in_8));
  Register #(.width(32)) register_39 (.D(in_4), .en(en6), .Q(O27), .clk(in_7), .clr(in_8));
  Register #(.width(32)) register_40 (.D(in_4), .en(en7), .Q(O31), .clk(in_7), .clr(in_8));
  D_Flip_Flop d_ff_1 (.clk(in_7), .D(Validate), .Q(V0), .en(en0), .reset(in_8));  // open: Qn, preset
  D_Flip_Flop d_ff_2 (.clk(in_7), .D(Validate), .Q(V1), .en(en1), .reset(in_8));  // open: Qn, preset
  D_Flip_Flop d_ff_3 (.clk(in_7), .D(Validate), .Q(V2), .en(en2), .reset(in_8));  // open: Qn, preset
  D_Flip_Flop d_ff_4 (.clk(in_7), .D(Validate), .Q(V3), .en(en3), .reset(in_8));  // open: Qn, preset
  D_Flip_Flop d_ff_5 (.clk(in_7), .D(Validate), .Q(V4), .en(en4), .reset(in_8));  // open: Qn, preset
  D_Flip_Flop d_ff_6 (.clk(in_7), .D(Validate), .Q(V5), .en(en5), .reset(in_8));  // open: Qn, preset
  D_Flip_Flop d_ff_7 (.clk(in_7), .D(Validate), .Q(V6), .en(en6), .reset(in_8));  // open: Qn, preset
  D_Flip_Flop d_ff_8 (.clk(in_7), .D(Validate), .Q(V7), .en(en7), .reset(in_8));  // open: Qn, preset
  Multiplexer #(.select(3), .width(32), .enable("false")) multiplexer_1 (
    .in0(O0), .in1(O4), .in2(O8), .in3(O12), .in4(O16), .in5(O20), .in6(O24), .in7(O28),
    .out(multiplexer_1_out), .sel(Addr[6:4]));
  Multiplexer #(.select(3), .width(32), .enable("false")) multiplexer_2 (
    .in0(O3), .in1(O7), .in2(O11), .in3(O15), .in4(O19), .in5(O23), .in6(O27), .in7(O31),
    .out(multiplexer_2_out), .sel(Addr[6:4]));
  Multiplexer #(.select(3), .enable("false")) multiplexer_3 (
    .in0(V0), .in1(V1), .in2(V2), .in3(V3), .in4(V4), .in5(V5), .in6(V6), .in7(V7), .out(Validated),
    .sel(Addr[6:4]));
  Comparator #(.width(13), .mode("unsigned")) comparator_1 (
    .a(TagCopy), .b(Addr[19:7]), .eq(comparator_1_eq));  // open: gt, lt
  Multiplexer #(.select(3), .width(32), .enable("false")) multiplexer_4 (
    .in0(O1), .in1(O5), .in2(O9), .in3(O13), .in4(O17), .in5(O21), .in6(O25), .in7(O29),
    .out(multiplexer_4_out), .sel(Addr[6:4]));
  Multiplexer #(.select(3), .width(32), .enable("false")) multiplexer_5 (
    .in0(O2), .in1(O6), .in2(O10), .in3(O14), .in4(O18), .in5(O22), .in6(O26), .in7(O30),
    .out(multiplexer_5_out), .sel(Addr[6:4]));
  and and_1 (Data_Ready, comparator_1_eq, Validated);
  Multiplexer #(.select(2), .width(32), .enable("false")) multiplexer_6 (
    .in0(multiplexer_1_out), .in1(multiplexer_4_out), .in2(multiplexer_5_out), .in3(multiplexer_2_out),
    .out({out_11[7:0], out_11[15:8], out_11[23:16], out_11[31:24]}), .sel(offset_t));
  not not_1 (not_1_out, Data_Ready);
  Multiplexer #(.select(3), .width(13), .enable("false")) multiplexer_7 (
    .in0(T0), .in1(T1), .in2(T2), .in3(T3), .in4(T4), .in5(T5), .in6(T6), .in7(T7), .out(TagCopy),
    .sel(Addr[6:4]));
  or or_1 (or_1_out, Ready_RT, Invalidate);
  Demultiplexer #(.select(3), .enable("false")) demultiplexer_1 (
    .out0(en0), .out1(en1), .out2(en2), .out3(en3), .out4(en4), .out5(en5), .out6(en6), .out7(en7),
    .in(or_1_out), .sel(multiplexer_8_out));
  Multiplexer #(.width(3), .enable("false")) multiplexer_8 (
    .in0(Addr[6:4]), .in1(W_Ram[2:0]), .out(multiplexer_8_out), .sel(in_9));
  Adder #(.width(4)) adder_1 (.a(RT), .out(adder_1_out));  // open: b, cin, cout
  D_Flip_Flop d_ff_9 (.clk(in_7), .D(not_1_out), .Q(d_ff_9_q));  // open: Qn, preset, en, reset
  Counter #(.width(4), .max('hf)) counter_1 (
    .load(not_1_out), .D(adder_1_out), .count(d_ff_9_q), .Q(counter_1_q), .clk(in_7));  // open: carry, clr
  Multiplexer #(.select(3), .width(13), .enable("false")) multiplexer_9 (
    .in0(T0), .in1(T1), .in2(T2), .in3(T3), .in4(T4), .in5(T5), .in6(T6), .in7(T7), .out(TagCopy_R),
    .sel(W_Ram[2:0]));
  nor nor_1 (nor_1_out, counter_1_q[0], counter_1_q[1], counter_1_q[2], counter_1_q[3]);
  Comparator #(.width(13), .mode("unsigned")) comparator_2 (
    .a(TagCopy_R), .b(W_Ram[15:3]), .eq(comparator_2_eq));  // open: gt, lt
  and and_2 (Ram, comparator_2_eq, Validated_R);
  nor nor_2 (Ram_Load, Data_Ready, in_8);
  and and_3 (Ready_RT, nor_1_out, d_ff_9_q);
  Multiplexer #(.select(3), .enable("false")) multiplexer_10 (
    .in0(V0), .in1(V1), .in2(V2), .in3(V3), .in4(V4), .in5(V5), .in6(V6), .in7(V7), .out(Validated_R),
    .sel(W_Ram[2:0]));
  and and_4 (Invalidate, in_9, Ram);
  not not_2 (Validate, Invalidate);

  assign out_12 = Addr[19:4];
  assign R_W_Ram = 1'b0;

  // Other names for the same wires on the sheet: OffSet[1:0] = Addr[3:2]; Addr_Ram[15:0] = Addr[19:4];
  //   Index[2:0] = Addr[6:4]; Tag[12:0] = Addr[19:7]; Clk = in_7; End_HIT = Data_Ready; IN0[31:0] = in_1;
  //   IN1[31:0] = in_2; IN2[31:0] = in_3; IN3[31:0] = in_4; Instruction[31:0] = out_11; R_W = in_9;
  //   Read_Ttime[3:0] = in_10; Reset = in_8; Index_Ram[2:0] = W_Ram[2:0]; Tag_Ram[12:0] = W_Ram[15:3]

  // Notes on the sheet:
  //   in_1: pull=down
  //   Addr: pull=down
  //   in_2: pull=down
  //   in_4: pull=down
  //   in_3: pull=down
  //   W_Ram: pull=down
  //   Inputs
  //   Tag
  //   Cache Memory
  //   Cache
  //   _____________________________________________________________________________
  //   _____________________________________________________________________________
  //   _____________________________________________________________________________
  //   _____________________________________________________________________________
  //   _____________________________________________________________________________
  //   _____________________________________________________________________________
  //   _____________________________________________________________________________
  //   Validate
  //   In Cache
  //   Read Time
  //   In Ram
  //   Outputs
endmodule

module Intruction_Decoder (
  input  [31:0] Intruction,
  output [31:0] Constant,
  output [25:0] Jump,
  output [3:0] Unit_Op,
  output [3:0] ALU_Op,
  output [2:0] Branch_Op,
  output [1:0] Special_Op,
  output [4:0] S_A,
  output [4:0] S_B,
  output [4:0] DA,
  output Move_Lo_Hi,
  output pop_push,
  output load_store
);

  wire add, addi, \and , and_1_out, and_32_out, and_33_out, andi, beq, bgtz, blez, bltz, bne, div, divu,
       halt, j, jr, kbd, lw, mfhi, mflo, mult, mulu, nop, \nor , \or , or_1_out, or_2_out, or_3_out,
       or_4_out, or_5_out, or_6_out, or_7_out, or_8_out, or_9_out, or_10_out, or_11_out, or_12_out,
       or_13_out, or_14_out, or_15_out, or_16_out, or_17_out, or_18_out, or_19_out, ori, pop, push, rnd, slt,
       slti, sltiu, sltu, sub, sw, tty, \xor , xori;
  wire [15:0] bit_extender_1_out;

  assign bit_extender_1_out = {{15{Intruction[15]}}, Intruction[15]};  // Bit_Extender bit_extender_1
  or or_1 (or_1_out, addi, slti, andi, ori, sltiu, xori);
  or or_2 (or_2_out, mult, mulu, div, divu);
  or or_3 (or_3_out, mflo, mfhi);
  or or_4 (or_4_out, beq, bltz, bne, j, blez, jr, bgtz);
  or or_5 (or_5_out, andi, xori, ori);
  Multiplexer #(.width(16), .enable("false")) multiplexer_1 (
    .in0(bit_extender_1_out), .in1({16{1'b0}}), .out(Constant[31:16]), .sel(or_5_out));
  or or_6 (or_6_out, add, \nor , sub, \xor , \and , slt, \or , sltu);
  or or_7 (or_7_out, pop, push);
  or or_8 (or_8_out, lw, sw);
  or or_9 (or_9_out, halt, tty, rnd, kbd);
  Priority_Encoder #(.select(4)) priority_encoder_1 (
    .in0(nop), .in1(or_6_out), .in2(or_1_out), .in3(or_2_out), .in4(or_3_out), .in5(or_7_out),
    .in6(or_4_out), .in7(or_8_out), .in8(or_9_out), .out(Unit_Op));  // open: in9, in10, in11, in12, in13, in14, in15, gs, en_out, en_in
  and and_1 (and_1_out, ~Intruction[26], ~Intruction[27], ~Intruction[28], ~Intruction[29], ~Intruction[30], ~Intruction[31]);  // AND_Gate
  or or_10 (or_10_out, lw, add, addi, sw);
  or or_11 (or_11_out, \and , andi);
  or or_12 (or_12_out, \or , ori);
  and and_2 (add, ~Intruction[0], ~Intruction[1], ~Intruction[2], and_1_out, ~Intruction[3], ~Intruction[4], Intruction[5]);  // AND_Gate
  and and_3 (sub, ~Intruction[0], Intruction[1], ~Intruction[2], and_1_out, ~Intruction[3], ~Intruction[4], Intruction[5]);  // AND_Gate
  and and_4 (mult, ~Intruction[0], ~Intruction[1], ~Intruction[2], and_1_out, Intruction[3], Intruction[4], ~Intruction[5]);  // AND_Gate
  and and_5 (mulu, Intruction[0], ~Intruction[1], ~Intruction[2], and_1_out, Intruction[3], Intruction[4], ~Intruction[5]);  // AND_Gate
  and and_6 (div, ~Intruction[0], Intruction[1], ~Intruction[2], and_1_out, Intruction[3], Intruction[4], ~Intruction[5]);  // AND_Gate
  and and_7 (divu, Intruction[0], Intruction[1], ~Intruction[2], and_1_out, Intruction[3], Intruction[4], ~Intruction[5]);  // AND_Gate
  or or_13 (or_13_out, \xor , xori);
  or or_14 (or_14_out, slt, slti);
  or or_15 (or_15_out, sltu, sltiu);
  or or_16 (or_16_out, blez, bgtz, bltz);
  Priority_Encoder #(.select(4)) priority_encoder_2 (
    .in0(mult), .in1(mulu), .in2(div), .in3(divu), .in4(or_10_out), .in5(sub), .in6(or_11_out),
    .in7(or_12_out), .in8(\nor ), .in9(or_13_out), .in10(or_14_out), .in11(or_15_out), .in12(or_16_out),
    .out(ALU_Op));  // open: in13, in14, in15, gs, en_out, en_in
  and and_8 (\and , ~Intruction[0], ~Intruction[1], Intruction[2], and_1_out, ~Intruction[3], ~Intruction[4], Intruction[5]);  // AND_Gate
  and and_9 (\or , Intruction[0], ~Intruction[1], Intruction[2], and_1_out, ~Intruction[3], ~Intruction[4], Intruction[5]);  // AND_Gate
  and and_10 (\nor , Intruction[0], Intruction[1], Intruction[2], and_1_out, ~Intruction[3], ~Intruction[4], Intruction[5]);  // AND_Gate
  and and_11 (\xor , ~Intruction[0], ~Intruction[1], ~Intruction[2], and_1_out, Intruction[3], ~Intruction[4], Intruction[5]);  // AND_Gate
  and and_12 (slt, ~Intruction[0], Intruction[1], ~Intruction[2], and_1_out, Intruction[3], ~Intruction[4], Intruction[5]);  // AND_Gate
  and and_13 (sltu, Intruction[0], Intruction[1], ~Intruction[2], and_1_out, Intruction[3], ~Intruction[4], Intruction[5]);  // AND_Gate
  Priority_Encoder priority_encoder_3 (
    .in0(beq), .in1(bne), .in2(blez), .in3(bgtz), .in4(bltz), .in5(j), .in6(jr), .in7(1'b1), .out(Branch_Op));  // open: en_in, gs, en_out
  Priority_Encoder #(.select(2)) priority_encoder_4 (
    .in0(halt), .in1(rnd), .in2(tty), .in3(kbd), .out(Special_Op));  // open: gs, en_out, en_in
  and and_14 (mfhi, ~Intruction[0], ~Intruction[1], ~Intruction[2], and_1_out, ~Intruction[3], Intruction[4], ~Intruction[5]);  // AND_Gate
  and and_15 (mflo, ~Intruction[0], Intruction[1], ~Intruction[2], and_1_out, ~Intruction[3], Intruction[4], ~Intruction[5]);  // AND_Gate
  and and_16 (nop, ~Intruction[0], ~Intruction[1], ~Intruction[2], and_1_out, ~Intruction[3], ~Intruction[4], ~Intruction[5]);  // AND_Gate
  and and_17 (jr, ~Intruction[0], ~Intruction[1], ~Intruction[2], and_1_out, Intruction[3], ~Intruction[4], ~Intruction[5]);  // AND_Gate
  Multiplexer #(.width(5), .enable("false")) multiplexer_2 (
    .in1(Intruction[25:21]), .out(S_A), .sel(or_17_out));  // open: in0
  or or_17 (or_17_out, add, sltu, sub, slti, mult, sltiu, mulu, beq, div, bne, divu, blez, addi, bgtz, bltz, \or , jr, \nor , lw, \xor , sw, andi, push, ori, tty, xori, \and , slt);
  and and_18 (addi, ~Intruction[26], ~Intruction[27], ~Intruction[28], Intruction[29], ~Intruction[30], ~Intruction[31]);  // AND_Gate
  and and_19 (andi, ~Intruction[26], ~Intruction[27], Intruction[28], Intruction[29], ~Intruction[30], ~Intruction[31]);  // AND_Gate
  and and_20 (ori, Intruction[26], ~Intruction[27], Intruction[28], Intruction[29], ~Intruction[30], ~Intruction[31]);  // AND_Gate
  and and_21 (xori, ~Intruction[26], Intruction[27], Intruction[28], Intruction[29], ~Intruction[30], ~Intruction[31]);  // AND_Gate
  and and_22 (slti, ~Intruction[26], Intruction[27], ~Intruction[28], Intruction[29], ~Intruction[30], ~Intruction[31]);  // AND_Gate
  and and_23 (sltiu, Intruction[26], Intruction[27], ~Intruction[28], Intruction[29], ~Intruction[30], ~Intruction[31]);  // AND_Gate
  Multiplexer #(.width(5)) multiplexer_3 (.in1(Intruction[20:16]), .out(S_B), .sel(or_18_out));  // open: in0, en
  or or_18 (or_18_out, add, \nor , sub, \xor , mult, slt, mulu, sltu, div, beq, divu, bne, \and , sw, \or );
  and and_24 (beq, ~Intruction[26], ~Intruction[27], Intruction[28], ~Intruction[29], ~Intruction[30], ~Intruction[31]);  // AND_Gate
  and and_25 (bne, Intruction[26], ~Intruction[27], Intruction[28], ~Intruction[29], ~Intruction[30], ~Intruction[31]);  // AND_Gate
  and and_26 (blez, ~Intruction[26], Intruction[27], Intruction[28], ~Intruction[29], ~Intruction[30], ~Intruction[31]);  // AND_Gate
  and and_27 (bgtz, Intruction[26], Intruction[27], Intruction[28], ~Intruction[29], ~Intruction[30], ~Intruction[31]);  // AND_Gate
  and and_28 (bltz, Intruction[26], ~Intruction[27], ~Intruction[28], ~Intruction[29], ~Intruction[30], ~Intruction[31]);  // AND_Gate
  and and_29 (j, ~Intruction[26], Intruction[27], ~Intruction[28], ~Intruction[29], ~Intruction[30], ~Intruction[31]);  // AND_Gate
  Multiplexer #(.width(5)) multiplexer_4 (
    .in0(Intruction[15:11]), .in1(Intruction[20:16]), .out(DA), .sel(or_19_out));  // open: en
  or or_19 (or_19_out, addi, slti, andi, sltiu, ori, lw, xori);
  and and_30 (lw, Intruction[26], Intruction[27], ~Intruction[28], ~Intruction[29], ~Intruction[30], Intruction[31]);  // AND_Gate
  and and_31 (sw, Intruction[26], Intruction[27], ~Intruction[28], Intruction[29], ~Intruction[30], Intruction[31]);  // AND_Gate
  Priority_Encoder #(.select(1)) priority_encoder_5 (
    .in0(mflo), .in1(mfhi), .out(Move_Lo_Hi));  // open: gs, en_out, en_in
  Priority_Encoder #(.select(1)) priority_encoder_6 (.in0(pop), .in1(push), .out(pop_push));  // open: gs, en_out, en_in
  Priority_Encoder #(.select(1)) priority_encoder_7 (.in0(lw), .in1(sw), .out(load_store));  // open: gs, en_out, en_in
  and and_32 (and_32_out, ~Intruction[26], ~Intruction[27], ~Intruction[28], Intruction[29], Intruction[30], Intruction[31]);  // AND_Gate
  and and_33 (and_33_out, Intruction[26], Intruction[27], Intruction[28], Intruction[29], Intruction[30], Intruction[31]);
  and and_34 (pop, ~Intruction[0], ~Intruction[1], ~Intruction[2], and_32_out, ~Intruction[3], ~Intruction[4], ~Intruction[5]);  // AND_Gate
  and and_35 (push, Intruction[0], ~Intruction[1], ~Intruction[2], and_32_out, ~Intruction[3], ~Intruction[4], ~Intruction[5]);  // AND_Gate
  and and_36 (halt, Intruction[0], Intruction[1], Intruction[2], and_33_out, Intruction[3], Intruction[4], Intruction[5]);
  and and_37 (tty, Intruction[0], ~Intruction[1], ~Intruction[2], and_33_out, ~Intruction[3], ~Intruction[4], ~Intruction[5]);  // AND_Gate
  and and_38 (rnd, ~Intruction[0], Intruction[1], ~Intruction[2], and_33_out, ~Intruction[3], ~Intruction[4], ~Intruction[5]);  // AND_Gate
  and and_39 (kbd, ~Intruction[0], ~Intruction[1], Intruction[2], and_33_out, ~Intruction[3], ~Intruction[4], ~Intruction[5]);  // AND_Gate

  assign Constant[15:0] = Intruction[15:0];
  assign Jump = Intruction[25:0];

  // Other names for the same wires on the sheet: Cons_Ext[31:0] = {Constant[31:16], Intruction[15:0]};
  //   Constant_t[15:0] = Intruction[15:0]; Destiny_Jump[25:0] = Intruction[25:0]; F1 = Intruction[0];
  //   Func_Code[5:0] = Intruction[5:0]; F2 = Intruction[1]; F3 = Intruction[2]; F4 = Intruction[3];
  //   F5 = Intruction[4]; F6 = Intruction[5]; Rd[4:0] = Intruction[15:11]; Rt[4:0] = Intruction[20:16];
  //   Rs[4:0] = Intruction[25:21]; O1 = Intruction[26]; Op_Code[5:0] = Intruction[31:26]; O2 = Intruction[27];
  //   O3 = Intruction[28]; O4 = Intruction[29]; O5 = Intruction[30]; O6 = Intruction[31]; Lo_Hi = Move_Lo_Hi

  // Notes on the sheet:
  //   Input
  //   Intruction Decoder
  //   Outputs
endmodule

module Branch_Control (
  input  [31:0] PC,
  input  [31:0] Const,
  input  [25:0] Destiny,
  input  N,
  input  Z,
  input  P,
  input  Equal,
  input  [2:0] B_Op,
  output [31:0] PC_out
);

  wire and_1_out;
  wire [1:0] J;
  wire [31:0] beq, bgtz, blez, bltz, bne, Const_Ext, Jump, Standar;

  Shifter #(.width(32)) shifter_1 (.in(Const), .\dist (5'b00010), .out(Const_Ext));
  and and_1 (and_1_out, N, Z);
  Multiplexer #(.width(32)) multiplexer_1 (.in0(Standar), .in1(Jump), .out(beq), .sel(Equal));  // open: en
  Multiplexer #(.width(32)) multiplexer_2 (.in0(Standar), .in1(Jump), .out(blez), .sel(and_1_out));  // open: en
  Adder #(.width(32)) adder_1 (.a(PC), .b(32'h4), .out(Standar));  // open: cin, cout
  Multiplexer #(.width(32)) multiplexer_3 (.in0(Jump), .in1(Standar), .out(bne), .sel(Equal));  // open: en
  Multiplexer #(.width(32)) multiplexer_4 (.in0(Standar), .in1(Jump), .out(bgtz), .sel(P));  // open: en
  Multiplexer #(.select(3), .width(32)) multiplexer_5 (
    .in0(beq), .in1(bne), .in2(blez), .in3(bgtz), .in4(bltz), .in5({PC[31:28], Destiny, J}), .in6(Const),
    .in7(Standar), .out(PC_out), .sel(B_Op));  // open: en
  Adder #(.width(32)) adder_2 (.a(Const_Ext), .b(Standar), .out(Jump));  // open: cin, cout
  Multiplexer #(.width(32)) multiplexer_6 (.in0(Standar), .in1(Jump), .out(bltz), .sel(N));  // open: en

  // Other names for the same wires on the sheet: J[31:2] = {PC[31:28], Destiny}

  // Notes on the sheet:
  //   N: pull=down
  //   Z: pull=down
  //   B_Op: pull=down
  //   Inputs
  //   Branch Control
  //   Outputs
endmodule

module Control_Unit (
  input  Inputs,
  input  in_2,
  input  in_3,
  input  in_4,
  input  in_5,
  input  in_6,
  input  [1:0] in_7,
  input  [3:0] in_8,
  input  [3:0] in_9,
  input  [3:0] in_10
);

  wire d_ff_1_q, demultiplexer_1_out0, demultiplexer_1_out1, IDLE_q, or_1_out, or_2_out;

  D_Flip_Flop IDLE (.clk(in_3), .D(demultiplexer_1_out0), .Q(IDLE_q), .preset(or_1_out));  // open: Qn, en, reset
  or or_1 (or_1_out, in_2, ~Inputs);  // OR_Gate
  Demultiplexer #(.enable("false")) demultiplexer_1 (
    .out0(demultiplexer_1_out0), .out1(demultiplexer_1_out1), .in(or_2_out), .sel(Inputs));
  buf or_2 (or_2_out, IDLE_q);  // OR_Gate
  D_Flip_Flop d_ff_1 (.clk(in_3), .D(demultiplexer_1_out1), .Q(d_ff_1_q), .reset(in_2));  // open: Qn, preset, en
  Demultiplexer #(.select(4), .enable("false")) demultiplexer_2 (
    .in(d_ff_1_q), .sel(in_8));  // open: out0, out1, out2, out3, out4, out5, out6, out7, out8, out9, out10, out11, out12, out13, out14, out15

  // Other names for the same wires on the sheet: Clk = in_3; End_Cache = in_5; Load_Store = in_6; Op[3:0] = in_8;
  //   P_P = in_4; R_Time[3:0] = in_9; Reset = in_2; Special_Op[1:0] = in_7; Start = Inputs; WTime[3:0] = in_10

  // Notes on the sheet:
  //   The Fucking Control Unit
endmodule
